// Logisim project vrc6_cells.circ as structural Verilog: 1 circuit, main circuit vrc6_31aoi
module vrc6_31aoi (
  input  a2,
  input  a1,
  input  b,
  input  a0,
  output x
);

  wire transistor_1_out, transistor_5_out, transistor_6_out;

  Transistor transistor_1 (.in(1'b1), .out(transistor_1_out), .gate(a2));
  Transistor transistor_2 (.in(1'b1), .out(transistor_1_out), .gate(a1));
  Transistor transistor_3 (.in(transistor_1_out), .out(x), .gate(b));
  Transistor transistor_4 (.in(transistor_1_out), .out(x), .gate(a0));
  Transistor #(.\type ("n")) transistor_5 (.in(1'b0), .out(transistor_5_out), .gate(a2));
  Transistor #(.\type ("n")) transistor_6 (.in(transistor_5_out), .out(transistor_6_out), .gate(a1));
  Transistor #(.\type ("n")) transistor_7 (.in(1'b0), .out(x), .gate(b));
  Transistor #(.\type ("n")) transistor_8 (.in(transistor_6_out), .out(x), .gate(a0));
endmodule
